// Logisim project logCircuit.circ as structural Verilog: 1 circuit, main circuit main
module main (
  input  R,
  input  in_2,
  input  IN,
  output Q,
  output out_5,
  output OUT
);

  wire not_1_out;

  not not_1 (not_1_out, IN);
  nor nor_1 (Q, R, out_5);
  nor nor_2 (out_5, Q, in_2);
  nand nand_1 (OUT, not_1_out, IN);

  // Notes on the sheet:
  //   S
  //   SR f/f
  //   G1
  //   G2
  //   NOT
  //   NAND
  //   ~Q
endmodule
